# Fritzing sketch Main base scheme (saved by Fritzing 0.9.3b)
breadboards: 1

parts:
  Arduino_Nano = Arduino Nano (Rev3.0)
  HC06 = Bluetooth HC-05 Macho
  OLED(I2C) = Grove OLED 128x96
  Кнопка = Momentary Switch [package=ksa_sealed_tac_switch]
  NRF24L01 = NRF24L01+ Breakout Board

nets:
  GND: Arduino_Nano.GND, HC06.GND, OLED(I2C).GND, Кнопка.3, NRF24L01.GND
  N1: Arduino_Nano.D2, HC06.TXD
  N2: Arduino_Nano.D3, HC06.RXD
  N3: Arduino_Nano.D4, Кнопка.2
  N4: Arduino_Nano.D7, NRF24L01.CE
  N5: Arduino_Nano.D8, NRF24L01.CS
  N6: Arduino_Nano.D11/MOSI, NRF24L01.MOSI
  N7: Arduino_Nano.D12/MISO, NRF24L01.MISO
  VCC: Arduino_Nano.5V, HC06.VCC, OLED(I2C).VCC
  N8: Arduino_Nano.A5, OLED(I2C).SCL
  N9: Arduino_Nano.A4, OLED(I2C).SDA
  3V3: Arduino_Nano.3V3, NRF24L01.VCC
  N10: Arduino_Nano.D13/SCK, NRF24L01.SCK
