# Fritzing sketch Remote node scheme (saved by Fritzing 0.9.3b)
breadboards: 1

parts:
  Часть1 = Arduino Nano (Rev3.0)
  Часть2 = NRF24L01+ Breakout Board
  S1 = Pushbutton [package="[THT]"]
  LED1 = RGB LED (com. cathode, rgb) [package="5 mm [THT]"]
  R1 = Resistor [tolerance=±5% resistance=220 package=THT]
  R2 = Resistor [tolerance=±5% resistance=220 package=THT]
  R3 = Resistor [tolerance=±5% resistance=220 package=THT]

nets:
  GND: Часть1.GND, Часть2.GND, S1.Pin_1, S1.Pin_2, LED1.common_cathode
  N1: Часть1.D2, S1.Pin_3, S1.Pin_4
  N2: Часть1.D7, Часть2.CE
  N3: Часть1.D8, Часть2.CS
  N4: Часть1.D11/MOSI, Часть2.MOSI
  N5: Часть1.D12/MISO, Часть2.MISO
  5V: Часть1.5V, Часть2.VCC
  N6: Часть1.A7, R1.Pin_0
  N7: Часть1.A6, R2.Pin_0
  N8: Часть1.A5, R3.Pin_0
  N9: Часть1.D13/SCK, Часть2.SCK
  N10: LED1.red_anode, R1.Pin_1
  N11: LED1.green_anode, R2.Pin_1
  N12: LED1.blue_anode, R3.Pin_1
